# Fritzing sketch esp8266-led-circuit-diagram (saved by Fritzing 0.9.4)
breadboards: 1

parts:
  R1 = Resistor [tolerance=±5% resistance=330 package=THT]
  LED1 = LED - 5mm [color="Red (633nm)" package="5 mm [THT]"]
  WeMos_D1_Mini1 = WeMos D1 Mini

nets:
  N1: R1.Pin_0, LED1.cathode
  N2: R1.Pin_1, WeMos_D1_Mini1.G
  N3: LED1.anode, WeMos_D1_Mini1.D1
